# Fritzing sketch MFA Mikel (saved by Fritzing 0.9.3b)
breadboards: 1

parts:
  Bauteil1 = Arduino Uno (Rev3)
  LCD1 = LCD screen
  Bauteil2 = 4x4 Keypad [part_number=101207]
  LED1 = LED - 5mm [color="Green (560nm)" package="5 mm [THT]"]
  LED2 = LED - 5mm [color="Red (633nm)" package="5 mm [THT]"]
  LCM1602_IIC1 = LCM1602 IIC [part_number="LCM1602 IIC" chip_label="LCM1602 IIC" package="DIP (Dual Inline) [THT]"]
  YwRobot_Power_Supply1 = YwRobot Breadboard Power Supply [part_number=545043]
  KF-1 = KF-301 Relay [package=THT]
  Bauteil3 = RFID-RC522 [part_number=101218]
  M1 = DC Motor
  R1 = Resistor [tolerance=±5% resistance=220 package=THT]
  R2 = Resistor [tolerance=±5% resistance=220 package=THT]

nets:
  N1: Bauteil1.A0, Bauteil2.8
  N2: Bauteil1.A1, Bauteil2.7
  N3: Bauteil1.A2, Bauteil2.6
  N4: Bauteil1.A3, Bauteil2.5
  N5: Bauteil1.A4/SDA, LCM1602_IIC1.SDA
  N6: Bauteil1.A5/SCL, LCM1602_IIC1.SCL
  N7: Bauteil1.D8, KF-1.signal
  N8: Bauteil1.D9_PWM, Bauteil3.RST
  N9: Bauteil1.D10_PWM/SS, Bauteil3.SDA
  N10: Bauteil1.D11_PWM/MOSI, Bauteil3.MOSI
  N11: Bauteil1.D12/MISO, Bauteil3.MISO
  N12: Bauteil1.D13/SCK, Bauteil3.SCK
  GND: Bauteil1.GND, LCM1602_IIC1.GND, YwRobot_Power_Supply1.GND#12, Bauteil3.GND, R1.Pin_1, R2.Pin_1
  N13: Bauteil1.D2, Bauteil2.4
  N14: Bauteil1.D3_PWM, Bauteil2.3
  N15: Bauteil1.D4, Bauteil2.2
  N16: Bauteil1.D5_PWM, Bauteil2.1
  N17: Bauteil1.D6_PWM, LED1.anode
  N18: Bauteil1.D7, LED2.cathode, LED2.anode, R1.Pin_0
  5V: Bauteil1.5V, LCM1602_IIC1.VCC, YwRobot_Power_Supply1.VCC#6
  VIN: Bauteil1.VIN, Bauteil3.3.3V
  VSS: LCD1.VSS, LCM1602_IIC1.VSS
  VDD: LCD1.VDD, LCM1602_IIC1.VDD
  N19: LCD1.V0, LCM1602_IIC1.V0
  N20: LCD1.RS, LCM1602_IIC1.RS
  N21: LCD1.R/W, LCM1602_IIC1.RW
  N22: LCD1.E, LCM1602_IIC1.E
  N23: LCD1.DB0, LCM1602_IIC1.D0
  N24: LCD1.DB1, LCM1602_IIC1.D1
  N25: LCD1.DB2, LCM1602_IIC1.D2
  N26: LCD1.DB3, LCM1602_IIC1.D3
  N27: LCD1.DB4, LCM1602_IIC1.D4
  N28: LCD1.DB5, LCM1602_IIC1.D5
  N29: LCD1.DB6, LCM1602_IIC1.D6
  N30: LCD1.DB7, LCM1602_IIC1.D7
  N31: LCD1.LED+, LCM1602_IIC1.A
  N32: LCD1.LED-, LCM1602_IIC1.K
  N33: LED1.cathode, R2.Pin_0
  N34: YwRobot_Power_Supply1.VCC#5, KF-1.power, M1.pin_2
  N35: YwRobot_Power_Supply1.GND#11, KF-1.ground, KF-1.C
  N36: KF-1.NC, M1.pin_1

custom parts:
  4x4 Keypad: Matrix membrane keypad 4x4
  LCM1602 IIC: I2C-Module to use a 1602 or 2004 LCD on with the wire.h libory Serial LCD Modul
  YwRobot Breadboard Power Supply: The YwRobot Breadboard Power Supply (MB-V2) has two power rails; they can be 5V or 3V3. Power to the module can be provided through the female USB socket or through the A10 (female) 2.1mm power jack.
  KF-301 Relay: KF-301
